# Fritzing sketch canary_controller (saved by Fritzing 0.9.3b)
breadboards: 1

parts:
  Part1 = Arduino Nano 33 IOT
  Part2 = Adafruit PCA9685 PWM/Servo Breakout [part_number=815]
  D1 = Rectifier Diode [part_number=1N4001 package="300 mil [THT]"]
  JACK1 = 2.1mm Barrel Jack with Terminal Block
  C2 = Ceramic Capacitor [capacitance=100nF package="200 mil [THT, multilayer]"]
  C3 = Ceramic Capacitor [capacitance=100nF package="200 mil [THT, multilayer]"]
  J1 = Basic Servo
  Part3 = Audio FX Sound Board + 2x2W Amp
  SP1 = SPEAKER [package=pcb_mount_speaker]  # not connected
  OLED1 = WaveShare 1.3 inch OLED
  U2 = Voltage Regulator - 5V [package="TO220 [THT]"]
  S1 = Pushbutton [package="[THT]"]
  S2 = Pushbutton [package="[THT]"]
  S3 = Pushbutton [package="[THT]"]
  R1 = Resistor [tolerance=±5% resistance=10k package=THT]
  R2 = Resistor [tolerance=±5% resistance=10k package=THT]

nets:
  N1: Part1.RX, Part3.TX
  N2: Part1.TX, Part3.RX
  N3: Part1.RESET, Part1.A7
  GND: Part1.GND, Part1.D13~, JACK1.NEG, C2.0, C3.1, Part3.GND, Part3.UG, OLED1.DIN, OLED1.GND, U2.GND, S1.Pin_1, S1.Pin_2, S2.Pin_1, S2.Pin_2, S3.Pin_1, S3.Pin_2
  N4: Part1.D2, S2.Pin_3, S2.Pin_4, R1.Pin_1
  N5: Part1.D3~, S3.Pin_3, S3.Pin_4, R2.Pin_1
  N6: Part1.D4, Part3.RST
  N7: Part1.D5~, OLED1.RES
  N8: Part1.D6~, OLED1.D/C
  N9: Part1.D7, OLED1.CS
  N10: Part1.D8, OLED1.CLK
  N11: Part1.D11/MOSI, Part1.+5V, OLED1.NC
  VIN: Part1.VIN, C3.0, Part3.VIN, U2.output_voltage
  3V3: Part1.3V3, OLED1.VCC, R1.Pin_0, R2.Pin_0
  N12: Part2.PWM0, J1.pulse
  N13: Part2.5.0V, J1.vcc
  GND_2: Part2.GND, J1.gnd
  N14: D1.cathode, C2.1, U2.input_voltage
  N15: D1.anode, JACK1.POS
  N16: S1.Pin_3, S1.Pin_4

notes:
  5V Servo
  9V DC Power supply
  L7805 5V Linear Regulator
  5V Rail !!!
  Nano 33 IoT
  3.3V !!!
  VCC
  GND
  DIN
  CLK
  CS
  DC
  RST
  BUSY
  330nF Ceramic
  100nF Ceramic
  1N4001
  LEFT
  RESET
  RIGHT
  10k pullups

custom parts:
  Arduino Nano 33 IOT: The Arduino Nano 33 IoT is the easiest and cheapest point of entry to enhance existing devices (and creating new ones) to be part of the IoT and designing pico-network applications. Whether you are looking at building a sensor network connected to your office or home router, or if you want to create a BLE device sending data to a cellphone, the Nano 33 IoT is your one-stop-solution for many of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
  Adafruit PCA9685 PWM/Servo Breakout: Using only two pins, control 16 free-running PWM outputs! I2C-controlled PWM driver with a built in clock. Unlike the TLC5940 family, you do not need to continuously send it signal tying up your microcontroller, its completely free running! 5V compliant, which means you can control it from a 3.3V microcontroller and still safely drive up to 6V outputs (this is good for when you want to control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
  Audio FX Sound Board + 2x2W Amp: The Adafruit Sound Board, the fastest way to add audio effects to a project!
  WaveShare 1.3 inch OLED: 128x64 Monochrom OLED Display with a SH1106 controller
